# Fritzing sketch schematic (saved by Fritzing 0.2.5)
breadboards: 1

parts:
  R1 = Basic Photo-Resistor (Photocell) [package=THT]
  R3 = 10k Ω Resistor [package=THT]
  C3 = Electrolytic Capacitor [package=THT]
  Arduino1 = Arduino Diecimila (deprecated) [package=THT]
  U1 = LM 358 Dual Op-Amp [package="DIP8 [THT]"]
  R12 = 33 Ω Resistor [package=THT]
  LED1 = Red LED - 5mm
  R14 = 47 Ω Resistor [package=THT]
  R15 = 220 Ω Resistor [package=THT]

nets:
  N1: R1.pin_0, Arduino1.+5V, U1.connector7, LED1.anode
  N2: R1.pin_1, R3.Pin_0, U1.connector2
  N3: R3.Pin_1, Arduino1.GND, U1.connector3, R12.Pin_0, R14.Pin_1
  N4: C3.-, R12.Pin_1
  N5: C3.+, Arduino1.A0, U1.connector0, R15.Pin_1
  N6: U1.connector1, R15.Pin_0
  N7: LED1.cathode, R14.Pin_0

notes:
  270 ohm
  10k ohm
  47 ohm
  100 microfarad
  1.8k ohm
