# Fritzing sketch heartmonitor (saved by Fritzing 0.2.3)
breadboards: 1

parts:
  R1 = Basic Photo-Resistor (Photocell) [package=THT]
  R3 = 10k Ω Resistor [package=THT]
  R7 = 10 Ω Resistor [package=THT]
  C3 = Electrolytic Capacitor [package=THT]
  R9 = 1.5k Ω Resistor [package=THT]
  C5 = Electrolytic Capacitor [package=THT]
  Arduino1 = Arduino Diecimila (deprecated) [package=THT]
  U1 = LM 358 Dual Op-Amp [package="DIP8 [THT]"]
  R12 = 33 Ω Resistor [package=THT]
  LED1 = Red LED - 5mm

nets:
  N1: R1.pin_0, R3.Pin_0, C3.-, R9.Pin_1
  N2: R1.pin_1, Arduino1.+5V, R12.Pin_1
  N3: R3.Pin_1, Arduino1.GND, LED1.cathode
  N4: R7.Pin_0, C5.+
  N5: R7.Pin_1, R9.Pin_0, C5.-, U1.connector0
  N6: Arduino1.A0, U1.connector6
  N7: R12.Pin_0, LED1.anode

notes:
  this is actually 1 ohm
  actually 1.8k ohm
